// Logisim project DDCA Project Expo, Team 07.circ as structural Verilog: 1 circuit, main circuit main
module main (
  input  in_1,
  input  in_2,
  input  in_3,
  output out_4
);

  wire not_1_out;

  not not_1 (not_1_out, in_2);
  and and_1 (out_4, in_1, not_1_out, in_3);
endmodule
